# Fritzing sketch plant_board_v01 (saved by Fritzing 0.9.3b)

parts:
  Part2 = Arduino Nano (Rev3.0)
  D_SENSE_1 = Diode [package=diode-1n4148]
  D_SENSE_2 = Diode [package=diode-1n4148]
  R_SENSE_2 = Resistor [tolerance=±5% resistance=20k package=THT]
  R_SENSE_1 = Resistor [tolerance=±5% resistance=20k package=THT]
  R_TEMP_1 = Resistor [tolerance=±5% resistance=1k package=THT]
  R1 = Resistor [tolerance=±5% resistance=10k package=THT]
  Q1 = NPN-Transistor [package="TO92 [THT]"]
  Q2 = NPN-Transistor [package="TO92 [THT]"]
  R2 = Resistor [tolerance=±5% resistance=10k package=THT]
  D_SENSE_3 = Diode [package=diode-1n4148]
  D_SENSE_4 = Diode [package=diode-1n4148]
  R_SENSE_4 = Resistor [tolerance=±5% resistance=20k package=THT]
  R_SENSE_5 = Resistor [tolerance=±5% resistance=20k package=THT]
  LED1 = LED - 5mm [color="Green (565nm)" package="5 mm [THT]"]
  R_LED_1 = Resistor [tolerance=±5% resistance=150 package=THT]
  LED2 = LED - 5mm [color="Green (565nm)" package="5 mm [THT]"]
  R_LED_2 = Resistor [tolerance=±5% resistance=150 package=THT]
  DS2 = DS18B20 1-Wire Temperature Sensor [part_number=DS18B20]
  DS3 = DS18B20 1-Wire Temperature Sensor [part_number=DS18B20]
  pump_2 = Screw terminal - 2 pins [package=THT]
  pump_1 = Screw terminal - 2 pins [package=THT]
  12V_input = Screw terminal - 2 pins [package=THT]
  SENS_2 = Screw terminal - 2 pins [package=THT]
  SENS_1 = Screw terminal - 2 pins [package=THT]
  I2C_BUS_IN = Screw terminal - 2 pins [package=THT]
  I2C_BUS_OUT = Screw terminal - 2 pins [package=THT]
  SHT21 = female pin header, 4 pins [form="♀ (female)"]

nets:
  GND: Part2.GND, R_SENSE_2.Pin_0, R_SENSE_1.Pin_0, Q1.E, Q2.E, R_SENSE_4.Pin_0, R_SENSE_5.Pin_0, R_LED_1.Pin_0, R_LED_2.Pin_0, DS2.GND, DS3.GND, 12V_input.pin2, SHT21.pin2
  N1: Part2.D2, D_SENSE_2.A
  N2: Part2.D3, D_SENSE_1.A, LED2.anode
  N3: Part2.D4, D_SENSE_3.A
  N4: Part2.D5, D_SENSE_4.A, LED1.anode
  N5: Part2.D6, R2.Pin_0
  N6: Part2.D7, R1.Pin_0
  N7: Part2.D12/MISO, R_TEMP_1.Pin_1, DS2.DQ, DS3.DQ
  12V: Part2.VIN, pump_2.pin1, pump_1.pin1, 12V_input.pin1
  5V: Part2.5V, R_TEMP_1.Pin_0, DS2.VDD, DS3.VDD, SHT21.pin1
  SCL (to D1): Part2.A5, I2C_BUS_IN.pin1, I2C_BUS_OUT.pin1, SHT21.pin3
  SDA (to D2): Part2.A4, I2C_BUS_IN.pin2, I2C_BUS_OUT.pin2, SHT21.pin4
  N8: Part2.A3, D_SENSE_2.C, R_SENSE_2.Pin_1, SENS_1.pin1
  N9: Part2.A2, D_SENSE_1.C, R_SENSE_1.Pin_1, SENS_1.pin2
  N10: Part2.A1, D_SENSE_3.C, R_SENSE_4.Pin_1, SENS_2.pin1
  N11: Part2.A0, D_SENSE_4.C, R_SENSE_5.Pin_1, SENS_2.pin2
  N12: R1.Pin_1, Q1.B
  N13: Q1.C, pump_1.pin2
  N14: Q2.B, R2.Pin_1
  N15: Q2.C, pump_2.pin2
  N16: LED1.cathode, R_LED_1.Pin_1
  N17: LED2.cathode, R_LED_2.Pin_1

notes:
  vcc
  gnd
